# Fritzing sketch ForceDetector (saved by Fritzing 0.9.2b)

parts:
  Part1 = Photon
  NEOPIXEL1 = Neopixel Strip -- Black (30/m)

nets:
  N1: Part1.A5, NEOPIXEL1.Din
  GND: Part1.GND, NEOPIXEL1.GND
  VIN: Part1.VIN, NEOPIXEL1.+5V

custom parts:
  Neopixel Strip -- Black (30/m): These NeoPixel strips have 30 digitally-addressable pixel LEDs per meter and are very affordable and are only 12.5 mm wide, 10 mm if you remove the strip from the casing.
